# Fritzing sketch dispenser_scheme (saved by Fritzing 0.9.3b)

parts:
  Часть1 = Arduino Mega 2560 (Rev3)
  GLCD_128x1 = 128 x 64 Graphic LCD
  Matrix_keypad1 = KEYPAD 4x4
  2_Channel_Relay1 = 2 Channel Power Relay
  2_Channel_Relay2 = 2 Channel Power Relay
  2_Channel_Relay3 = 2 Channel Power Relay
  2_Channel_Relay4 = 2 Channel Power Relay
  J1 = Piezo Speaker
  Часть2 = HX711 Weighing Sensor Module

nets:
  GND: Часть1.GND, GLCD_128x1.1_Vss, GLCD_128x1.15_CS1, GLCD_128x1.20_K(-), 2_Channel_Relay1.GND, 2_Channel_Relay2.GND, 2_Channel_Relay3.GND, 2_Channel_Relay4.GND, J1.pin1, Часть2.GND
  N1: Часть1.D11_PWM, Matrix_keypad1.col1
  N2: Часть1.D10_PWM, Matrix_keypad1.col2
  N3: Часть1.D9_PWM, Matrix_keypad1.col3
  N4: Часть1.D8_PWM, Matrix_keypad1.col4
  N5: Часть1.3V3, GLCD_128x1.19_A(+)
  VCC: Часть1.5V, GLCD_128x1.2_Vdd, 2_Channel_Relay1.VCC, 2_Channel_Relay2.VCC, 2_Channel_Relay3.VCC, 2_Channel_Relay4.VCC, Часть2.VCC
  N6: Часть1.D3_PWM, J1.pin2
  N7: Часть1.D4_PWM, Matrix_keypad1.row4
  N8: Часть1.D5_PWM, Matrix_keypad1.row3
  N9: Часть1.D6_PWM, Matrix_keypad1.row2
  N10: Часть1.D7_PWM, Matrix_keypad1.row1
  N11: Часть1.D31, 2_Channel_Relay1.IN1
  N12: Часть1.D32, 2_Channel_Relay1.IN2
  N13: Часть1.D33, 2_Channel_Relay2.IN1
  N14: Часть1.D34, 2_Channel_Relay2.IN2
  N15: Часть1.D35, 2_Channel_Relay3.IN1
  N16: Часть1.D36, 2_Channel_Relay3.IN2
  N17: Часть1.D37, 2_Channel_Relay4.IN1
  N18: Часть1.D38, 2_Channel_Relay4.IN2
  N19: Часть1.D48, Часть2.CK/TX
  N20: Часть1.D49, Часть2.DO/RX
  N21: Часть1.D51, GLCD_128x1.5_R/W
  N22: Часть1.D52, GLCD_128x1.6_Enable
  N23: Часть1.D53, GLCD_128x1.4_D/I

notes:
  1
  2
  3
  4
  7
  8
  6
  5

custom parts:
  KEYPAD 4x4: Matrix keypad 16 buttons, 4 rows x 4 columns
  2 Channel Power Relay: A 2 channel power relay. The module operates at 5V.
